# Fritzing sketch Interupt (saved by Fritzing 0.9.9b)
breadboards: 1

parts:
  J1 = STM32 Nucleo boards
  LED1 = LED - 5mm [color="Red (633nm)" current=0.030 package="5 mm [THT]"]
  S1 = Pushbutton [package="[THT]"]

nets:
  N1: J1.D4, LED1.anode
  N2: J1.D6_PWM, S1.Pin_3, S1.Pin_4
  N3: J1.3V3, S1.Pin_1, S1.Pin_2
  N4: J1.GND, LED1.cathode
