# Fritzing sketch pwm_led (saved by Fritzing 0.9.9b)
breadboards: 1

parts:
  J1 = STM32 Nucleo boards
  LED1 = LED - 5mm [color="Red (633nm)" current=0.030 package="5 mm [THT]"]
  R1 = Resistor [tolerance=±5% power=0.25 resistance=220 package=THT]

nets:
  N1: J1.A0, R1.Pin_0
  N2: J1.GND, LED1.anode
  N3: LED1.cathode, R1.Pin_1
